// Logisim project A.circ as structural Verilog: 1 circuit, main circuit main
module main (
  input  in_1
);

  wire [7:0] undriven;

  Comparator comparator_1 (.a(undriven), .b(undriven));  // open: gt, eq, lt
endmodule
